# Fritzing sketch stage project monitoring alim maser (saved by Fritzing 0.9.3b)
breadboards: 1

parts:
  Composant1 = Arduino Uno (Rev3) - ICSP
  R1 = Resistor [tolerance=±5% resistance=10k package="0402 [SMD]"]
  R2 = Resistor [tolerance=±5% resistance=10k package="2010 [SMD]"]
  R3 = Resistor [tolerance=±5% resistance=10k package="2512 [SMD]"]
  R4 = Resistor [tolerance=±5% resistance=220 package=THT]
  R5 = Resistor [tolerance=±5% resistance=220 package=THT]
  R6 = Resistor [tolerance=±5% resistance=220 package=THT]
  IC1 = Voltage Regulator [package=to220-igo]
  U2 = RELAY [package=relay-g5q]
  OMRON1 = OMRON PCB Power Relay – G5LE [part_number="G5LE-1\n" package=THT]  # not connected
  C1 = Electrolytic Capacitor [capacitance=10μF package="0605 [SMD, electrolytic]"]
  C2 = Electrolytic Capacitor [capacitance=1000μF package="1010 [SMD, electrolytic]"]
  VCC1 = Battery block 9V  # not connected

nets:
  N1: Composant1.D9_PWM, R2.Pin_1
  N2: Composant1.D3_PWM, U2.COIL2
  N3: Composant1.D6_PWM, R1.Pin_0
  N4: Composant1.5V, R4.Pin_0
  N5: Composant1.GND, R1.Pin_1, R2.Pin_0, R3.Pin_1, IC1.IN, C1.-
  N6: R4.Pin_1, R6.Pin_0
  N7: R5.Pin_0, R6.Pin_1
  N8: IC1.GND, C1.+
  N9: IC1.OUT, C2.+

notes:
  MASER
  AC/DC
  DIODE
  Backup 26V
  DC/DC
  2F
  15V
  30V
  12V
