# Fritzing sketch stage project monitoring alim maser2 (saved by Fritzing 0.9.3b)
breadboards: 1

parts:
  Composant1 = Arduino Uno (Rev3) - ICSP
  R1 = Resistor [tolerance=±5% resistance=10k package="0402 [SMD]"]
  R2 = Resistor [tolerance=±5% resistance=10k package="2010 [SMD]"]
  R3 = Resistor [tolerance=±5% resistance=10k package="2512 [SMD]"]
  R4 = Resistor [tolerance=±5% resistance=220 package=THT]
  R5 = Resistor [tolerance=±5% resistance=220 package=THT]
  R6 = Resistor [tolerance=±5% resistance=220 package=THT]

nets:
  N1: Composant1.D9_PWM, R2.Pin_1
  N2: Composant1.D10_PWM/SS, R5.Pin_1
  N3: Composant1.D4, R3.Pin_0
  N4: Composant1.D5_PWM, R6.Pin_1
  N5: Composant1.D6_PWM, R1.Pin_0
  N6: Composant1.D7, R4.Pin_1
  N7: Composant1.GND, R1.Pin_1, R2.Pin_0, R3.Pin_1

notes:
  MASER
  AC/DC
  DIODE
  Backup 26V
  DC/DC
  2F
  30V
  15V
  12V
  ~230V
  10kΩ
  220kΩ
  input B
  output B
  input A
  output A
  output
  input
