# Fritzing sketch stage project monitoring alim maser3 (saved by Fritzing 0.9.3b)
breadboards: 1

parts:
  Composant1 = Arduino Uno (Rev3) - ICSP
  R3 = Resistor [tolerance=±5% resistance=10k package="2512 [SMD]"]
  R5 = Resistor [tolerance=±5% resistance=220 package=THT]
  R6 = Resistor [tolerance=±5% resistance=220 package=THT]
  D1 = Rectifier Diode [part_number=1N4001 package="300 mil [THT]"]
  D2 = Rectifier Diode [part_number=1N4001 package="300 mil [THT]"]
  D3 = Rectifier Diode [part_number=1N4001 package="300 mil [THT]"]
  R7 = Resistor [tolerance=±5% resistance=220 package=THT]
  S1 = Pushbutton [package="[SMD]"]
  R8 = Resistor [tolerance=±5% resistance=10k package="2512 [SMD]"]
  C1 = Ceramic Capacitor [capacitance="100 nF" package="0805 [SMD, multilayer]"]

nets:
  N1: Composant1.D8, S1.Pin_3, S1.Pin_4, R8.Pin_0, C1.0
  N2: Composant1.D2, R6.Pin_1, D3.cathode
  N3: Composant1.D4, D2.cathode, R7.Pin_0
  N4: Composant1.D6_PWM, R5.Pin_1, D1.cathode
  N5: Composant1.5V, R8.Pin_1
  N6: Composant1.GND, R3.Pin_0, S1.Pin_1, S1.Pin_2, C1.1
  N7: R3.Pin_1, D1.anode, D2.anode, D3.anode

notes:
  MASER
  AC/DC
  DIODE
  Backup 26V
  DC/DC
  2F
  30V
  15V
  12V
  ~230V
  10kΩ
  220kΩ
  input B
  output B
  input A
  output A
  output
  input
  10nF
